// Logisim project ISA_12Bits.circ as structural Verilog
module Banco_de_Resgistradores (
  input  [11:0] rs1_out,
  input  [2:0] rs1,
  input  [11:0] rs2_out,
  input  [2:0] rd,
  input  regWrite,
  input  [2:0] rs2,
  input  [11:0] wdata
);

  wire and_1_out, and_2_out, and_3_out, and_4_out, and_5_out, and_6_out, and_7_out;
  wire [11:0] demultiplexer_1_out1, demultiplexer_1_out3, demultiplexer_1_out7, R0_q, R1_q, R2_q, R3_q, R4_q,
       R5_q, R6_q, R7_q;
  wire [11:1] undriven;

  Demultiplexer #(.select(3), .width(12)) demultiplexer_1 (
    .out1(demultiplexer_1_out1), .out2(demultiplexer_1_out1), .out3(demultiplexer_1_out3),
    .out4(demultiplexer_1_out3), .out5(demultiplexer_1_out3), .out6(demultiplexer_1_out3),
    .out7(demultiplexer_1_out7), .in({undriven, regWrite}), .sel(rd));  // open: out0
  and and_1 (and_1_out, regWrite, demultiplexer_1_out1[0]);
  and and_2 (and_2_out, regWrite, demultiplexer_1_out1[0]);
  and and_3 (and_3_out, regWrite, demultiplexer_1_out3[0]);
  and and_4 (and_4_out, regWrite, demultiplexer_1_out3[0]);
  and and_5 (and_5_out, regWrite, demultiplexer_1_out3[0]);
  and and_6 (and_6_out, regWrite, demultiplexer_1_out3[0]);
  and and_7 (and_7_out, regWrite, demultiplexer_1_out7[0]);
  Register #(.width(12)) R0 (.D(wdata), .en(1'b0), .Q(R0_q));  // open: clk, clr
  Register #(.width(12)) R1 (.D(wdata), .en(and_1_out), .Q(R1_q));  // open: clk, clr
  Register #(.width(12)) R2 (.D(wdata), .en(and_2_out), .Q(R2_q));  // open: clk, clr
  Register #(.width(12)) R3 (.D(wdata), .en(and_3_out), .Q(R3_q));  // open: clk, clr
  Register #(.width(12)) R4 (.D(wdata), .en(and_4_out), .Q(R4_q));  // open: clk, clr
  Register #(.width(12)) R5 (.D(wdata), .en(and_5_out), .Q(R5_q));  // open: clk, clr
  Register #(.width(12)) R6 (.D(wdata), .en(and_6_out), .Q(R6_q));  // open: clk, clr
  Register #(.width(12)) R7 (.D(wdata), .en(and_7_out), .Q(R7_q));  // open: clk, clr
  Multiplexer #(.select(3), .width(12)) multiplexer_1 (
    .in0(R0_q), .in1(R1_q), .in2(R2_q), .in3(R3_q), .in4(R4_q), .in5(R5_q), .in6(R6_q), .in7(R7_q),
    .out(rs1_out), .sel(rs1));
  Multiplexer #(.select(3), .width(12)) multiplexer_2 (
    .in0(R0_q), .in1(R1_q), .in2(R2_q), .in3(R3_q), .in4(R4_q), .in5(R5_q), .in6(R6_q), .in7(R7_q),
    .out(rs2_out), .sel(rs2));
  Demultiplexer demultiplexer_2 ();  // open: out0, out1, in, sel
  Multiplexer #(.select(2), .width(12)) multiplexer_3 ();  // open: in0, in1, in2, in3, out, sel
  // Pins of 1 and 12 bits meet at {undriven, regWrite}
  // Pins of 1 and 12 bits meet at demultiplexer_1_out1
  // Pins of 1 and 12 bits meet at demultiplexer_1_out3
  // Pins of 1 and 12 bits meet at demultiplexer_1_out7
endmodule

module ULA (
  input  [3:0] ULAop,
  input  [11:0] A,
  input  Result,
  input  [11:0] B,
  input  zero,
  input  [11:0] B_data,
  input  [4:0] B_imm,
  input  ULAsrc
);

  wire [11:0] bit_extender_1_out;
  wire [11:1] adder_1_out;

  assign bit_extender_1_out = {{7{B_imm[4]}}, B_imm};  // Bit_Extender bit_extender_1
  Multiplexer #(.select(2), .width(12)) multiplexer_1 (
    .in2(bit_extender_1_out), .in3(B_data), .out(A));  // open: in0, in1, sel
  Comparator comparator_1 (.a(A[7:0]), .b(A[7:0]), .lt(Result));  // open: gt, eq
  Adder #(.width(12)) adder_1 (.a(A), .out({adder_1_out, Result}));  // open: b, cin, cout
  // OR_Gate or_1 has open pins: in0=A[0], in1=A[0], out=open
  // OR_Gate or_2 has open pins: in0=A[0], in1=A[0], out=open
  // OR_Gate or_3 has open pins: in0=A[0], in1=A[0], out=open
  // OR_Gate or_4 has open pins: in0=A[0], in1=A[0], out=open
  // XOR_Gate xor_1 has open pins: in0=A[0], in1=A[0], out=open
  // XOR_Gate xor_2 has open pins: in0=A[0], in1=A[0], out=open
  // XOR_Gate xor_3 has open pins: in0=A[0], in1=A[0], out=open
  // XOR_Gate xor_4 has open pins: in0=A[0], in1=A[0], out=open
  // AND_Gate and_1 has open pins: in0=A[0], in1=A[0], out=open
  // AND_Gate and_2 has open pins: in0=A[0], in1=A[0], out=open
  // AND_Gate and_3 has open pins: in0=A[0], in1=A[0], out=open
  // AND_Gate and_4 has open pins: in0=A[0], in1=A[0], out=open
  // AND_Gate and_5 has open pins: in0=A[0], in1=A[0], out=open
  // AND_Gate and_6 has open pins: in0=A[0], in1=A[0], out=open
  // AND_Gate and_7 has open pins: in0=A[0], in1=A[0], out=open
  // AND_Gate and_8 has open pins: in0=A[0], in1=A[0], out=open
  // OR_Gate or_5 has open pins: in0=A[0], in1=A[0], out=open
  // OR_Gate or_6 has open pins: in0=A[0], in1=A[0], out=open
  // OR_Gate or_7 has open pins: in0=A[0], in1=A[0], out=open
  // OR_Gate or_8 has open pins: in0=A[0], in1=A[0], out=open
  // XOR_Gate xor_5 has open pins: in0=A[0], in1=A[0], out=open
  // XOR_Gate xor_6 has open pins: in0=A[0], in1=A[0], out=open
  // XOR_Gate xor_7 has open pins: in0=A[0], in1=A[0], out=open
  // XOR_Gate xor_8 has open pins: in0=A[0], in1=A[0], out=open
  // AND_Gate and_9 has open pins: in0=A[0], out=open
  // AND_Gate and_10 has open pins: in0=A[0], in1=A[0], out=open
  // AND_Gate and_11 has open pins: in0=A[0], in1=A[0], out=open
  // AND_Gate and_12 has open pins: in0=A[0], in1=A[0], out=open
  // OR_Gate or_9 has open pins: in0=A[0], in1=A[0], out=open
  // OR_Gate or_10 has open pins: in0=A[0], in1=A[0], out=open
  // OR_Gate or_11 has open pins: in0=A[0], out=open
  // OR_Gate or_12 has open pins: in0=A[0], in1=A[0], out=open
  // XOR_Gate xor_9 has open pins: in0=A[0], in1=A[0], out=open
  // XOR_Gate xor_10 has open pins: in0=A[0], in1=A[0], out=open
  // XOR_Gate xor_11 has open pins: in0=A[0], in1=A[0], out=open
  // XOR_Gate xor_12 has open pins: in0=A[0], in1=A[0], out=open
  Multiplexer #(.select(3), .width(12)) multiplexer_2 ();  // open: in0, in1, in2, in3, in4, in5, in6, in7, out, sel
  // Pins of 1 and 8 and 12 bits meet at A
  // Pins of 1 and 12 bits meet at {adder_1_out, Result}

  assign B = A;
endmodule

module MemInst (
);

  ROM #(.addrWidth(12), .dataWidth(12)) rom_1 ();  // open: addr, data
endmodule

module PC (
  input  PC_out,
  input  Target,
  input  Jump
);

  wire [11:0] adder_1_out, multiplexer_1_out;
  wire [11:1] undriven, undriven_2;

  Register #(.width(12)) R1 (.D(multiplexer_1_out));  // open: en, clk, Q, clr
  Adder #(.width(12)) adder_1 (.a(12'h2), .b({undriven_2, PC_out}), .out(adder_1_out));  // open: cin, cout
  Multiplexer #(.width(12)) multiplexer_1 (
    .in0(adder_1_out), .in1({undriven, Target}), .out(multiplexer_1_out), .sel(Jump));
  // Pins of 1 and 12 bits meet at {undriven, Target}
  // Pins of 1 and 12 bits meet at {undriven_2, PC_out}
endmodule

module DecodInst (
  input  [11:0] A,
  input  [11:0] b,
  input  [3:0] sel
);
endmodule
